# Fritzing sketch lightom (saved by Fritzing 0.9.0b)
breadboards: 1

parts:
  Part1 = Arduino Uno (Rev3)
  R1 = Resistor [tolerance=±5% resistance=220 package=THT]
  D1 = Rectifier Diode [part_number=1N4001 package="300 mil [THT]"]
  Q1 = NPN-Transistor [package="TO92 [THT]"]
  K1 = Relay [part_number=FRS1B-S package=THT]
  LED1 = LED - 5mm [color="Red (633nm)" package="5 mm [THT]"]
  LED2 = LED - 5mm [color="Red (633nm)" package="5 mm [THT]"]
  LED3 = LED - 5mm [color="Red (633nm)" package="5 mm [THT]"]
  LED4 = LED - 5mm [color="Red (633nm)" package="5 mm [THT]"]
  U1 = XBee
  VCC1 = Battery  # not connected
  R2 = Resistor [tolerance=±5% resistance=220 package=THT]
  R3 = Photocell (LDR) [package=THT]
  R4 = Resistor [tolerance=±5% resistance=220 package=THT]
  U4 = TMP36 [package=to-92-kit]

nets:
  N1: Part1.A0, R2.Pin_1, R3.pin_0
  N2: Part1.A1, R4.Pin_1, U4.VOUT
  N3: Part1.D8, U1.pin19
  N4: Part1.D2, R1.Pin_0
  N5: Part1.D7, U1.pin20
  5V: Part1.5V, D1.cathode, K1.COIL1, U1.VCC, R2.Pin_0, R4.Pin_0
  GND: Part1.GND, Q1.C, U1.GND, R3.pin_1, U4.GND
  N6: R1.Pin_1, Q1.B
  N7: D1.anode, Q1.E, K1.COIL2
  N8: K1.A, LED1.anode, LED2.anode, LED3.anode, LED4.anode
  N9: K1.C1, K1.C2
  N10: K1.B, LED1.cathode, LED2.cathode, LED3.cathode, LED4.cathode
